# Fritzing sketch DTH22 (saved by Fritzing 0.9.3b)

parts:
  U1 = ESP8266 WiFi Module [part_number=ESP8266]
  DHT22 = DHT22 Humidity and Temperature Sensor
  VCC1 = Battery
  R1 = Resistor [tolerance=±5% resistance=10k package=THT]

nets:
  VCC: U1.VCC, U1.CH_PD, DHT22.VDD, VCC1.+, R1.Pin_1
  N1: U1.GPIO_0, DHT22.DATA, R1.Pin_0
  GND: U1.GND, DHT22.GND, VCC1.-

notes:
  VCC
  RESET
  CH_PD
  TX
  RX
  GND
  GPIO 2
  GPIO 0

custom parts:
  ESP8266 WiFi Module: Generic WiFi Module based on the ESP8266 with onboard PCB antenna and UART communications
